# Fritzing sketch schematic (saved by Fritzing 0.9.0b)

parts:
  Arduino2 = Arduino Uno (Rev3)
  LED2 = LEDs [package=led10mm]

nets:
  N1: Arduino2.GND, LED2.A

notes:
  No resistor if the Arduino is powered by USB!
